# Fritzing sketch Schematic (saved by Fritzing 0.9.3b)
circuit board: 3.61693cm x 2.22035cm
breadboards: 1

parts:
  J1 = Piezo Speaker
  VCC1 = 4 x AAA Battery Mount
  S1 = Toggle Switch [package=THT]
  U1 = attiny85 [package=dip]

nets (from the schematic view):
  N1: J1.pin1, VCC1.-, U1.Pin_4
  N2: J1.pin2, U1.Pin_6
  N3: VCC1.+, S1.COM
  N4: S1.L2, U1.Pin_8

notes:
  Use a 3V coin battery to save space
